# Fritzing sketch fritzing_layouts (saved by Fritzing 0.9.4)
breadboards: 1

parts:
  DHT1 = DHT22 Humidity and Temperature Sensor
  R1 = Resistor [tolerance=±5% resistance=10k package=THT]
  LED1 = smd LED [color="Red (633nm)" package="0805 [SMD]"]
  LED2 = smd LED [color="Green (555nm)" package="0805 [SMD]"]
  R2 = Resistor [tolerance=±5% resistance=1k package=THT]
  R3 = Resistor [tolerance=±5% resistance=1k package=THT]
  U2 = ESP32S-HiLetgo [part_number=ESP32S-HiLetgo]
  Part1 = LCD1602-I2C

nets:
  VDD: DHT1.VDD, R1.Pin_1, U2.VIN, Part1.VCC
  N1: DHT1.DATA, R1.Pin_0, U2.GPIO4
  GND: DHT1.GND, LED1.cathode, LED2.cathode, U2.GND, Part1.GND
  N2: LED1.anode, R2.Pin_0
  N3: LED2.anode, R3.Pin_0
  N4: R2.Pin_1, U2.GPIO16
  N5: R3.Pin_1, U2.GPIO17
  N6: U2.GPIO21, Part1.SDA
  N7: U2.GPIO22, Part1.SCL

notes:
  5V
  GPIO17
  GPIO16
  GPIO4

custom parts:
  ESP32S-HiLetgo: HiLetgo ESP-WROOM-32 ESP32 ESP-32S Development Board 2.4GHz Dual-Mode WiFi + Bluetooth Dual Cores Microcontroller The ESP32 integrated with Antenna switches, RF Balun, power amplifiers, low-noise amplifiers, filters, and management modules, and the entire solution occupies the least area of PCB. 2.4 GHz Wi-Fi plus Bluetooth dual-mode chip, with TSMC Ultra-low power consumption 40nm technology,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
  LCD1602-I2C: A standard character display, usually with 2x16 characters. Comes in many colors with LCM1602 IIC attached.
